# Fritzing sketch PIR (saved by Fritzing 0.9.3b)
circuit board: 8.46667cm x 5.64444cm
breadboards: 1

parts:
  J1 = Camdenboss CTB0158-4 [part_number=CTB0158-4 package=THT]
  NANO = Arduino Nano (Rev3.0)
  R1 = Resistor [tolerance=±5% resistance=10k package=THT]
  XBEE = XBee Explorer Regulated

nets:
  N1: J1.pin1, NANO.VIN
  GND: J1.pin2, NANO.GND, XBEE.GND
  N2: J1.pin3, NANO.5V
  N3: J1.pin4, NANO.D3
  N4: NANO.D5, R1.Pin_1, XBEE.DTR
  N5: NANO.D7, XBEE.DIN
  N6: NANO.D9, XBEE.DOUT
  3V3: NANO.3V3, R1.Pin_0, XBEE.3.3V
