# Fritzing sketch detectorbeacons (saved by Fritzing 0.9.3b)
circuit board: 10.0429cm x 5.65554cm
breadboards: 1

parts:
  xbee = XBee Explorer Regulated
  Componente2 = Arduino Uno (Rev3) - ICSP
  BT_MH-10 = Bluetooth HC-05 Macho

nets:
  N1: xbee.DIN, Componente2.D7
  N2: xbee.DOUT, Componente2.D5_PWM
  3.3V: xbee.3.3V, Componente2.3V3, BT_MH-10.VCC
  GND: xbee.GND, Componente2.GND, BT_MH-10.GND
  N3: Componente2.ICSP_MOSI, Componente2.D11_PWM/MOSI, BT_MH-10.RXD
  N4: Componente2.D9_PWM, BT_MH-10.TXD
