# Fritzing sketch tento_nevera_sensor (saved by Fritzing 0.9.3b)
circuit board: 8.2705cm x 5.76433cm
breadboards: 1

parts:
  A_NANO = Arduino Nano (Rev3.0)
  PHOTOCELL = PHOTOCELL [package=photocell-kit]
  TEMPERATURE = DS18B20 1-Wire Temperature Sensor [part_number=DS18B20]
  R1 = Resistor [tolerance=±5% resistance=10k package=THT]
  R2 = Resistor [tolerance=±5% resistance=4.7k package=THT]
  XBEE = XBee Explorer Regulated
  hc-sr04 = hc-sr04
  J1 = Camdenboss CTB0158-2 [part_number=CTB0158-2 package=THT]
  R3 = Resistor [tolerance=±5% resistance=10k package=THT]

nets:
  GND: A_NANO.GND, PHOTOCELL.P$1, TEMPERATURE.GND, XBEE.GND, hc-sr04.GND, J1.pin2
  N1: A_NANO.D2, XBEE.DOUT
  N2: A_NANO.D3, XBEE.DIN
  N3: A_NANO.D4, XBEE.DTR, R3.Pin_1
  N4: A_NANO.D5, hc-sr04.Trig
  N5: A_NANO.D7, hc-sr04.Echo
  N6: A_NANO.D9, TEMPERATURE.DQ, R2.Pin_1
  N7: A_NANO.VIN, J1.pin1
  5V: A_NANO.5V, TEMPERATURE.VDD, R1.Pin_0, R2.Pin_0, hc-sr04.VCC
  N8: A_NANO.A6, PHOTOCELL.P$2, R1.Pin_1
  3V3: A_NANO.3V3, XBEE.3.3V, R3.Pin_0
